# Fritzing sketch Bubbles (saved by Fritzing 0.9.4)
circuit board: 10cm x 8cm

parts:
  IC = WeMos D1 Mini
  5v_Power = Camdenboss CTB0158-2 [part_number=CTB0158-2 package=THT]
  R1 = Resistor [tolerance=±5% resistance=220 package=THT]
  R2 = Resistor [tolerance=±5% resistance=100 package=THT]
  R3 = Resistor [tolerance=±5% resistance=10k package=THT]
  3_3v_Relay = OMRON PCB Power Relay – G5LE [part_number="G5LE-1\r\n" package=THT]
  Relay_Out = Camdenboss CTB0158-3 [part_number=CTB0158-3 package=THT]
  Status = LED - 3mm [color="Red (633nm)" package="3 mm [THT]"]
  Power = LED - 3mm [color="Red (633nm)" package="3 mm [THT]"]
  Pwr = SPST Switch [package=switch-spdt]
  3v_<->_5v = Logic Level Converter
  5v_Logic = Camdenboss CTB0158-4 [part_number=CTB0158-4 package=THT]
  J1 = Camdenboss CTB0158-8 [part_number=CTB0158-8 package=THT]
  Input = Momentary Switch [package=ksa_sealed_tac_switch]
  J2 = Camdenboss CTB0158-8 [part_number=CTB0158-8 package=THT]

nets:
  N1: IC.3V3, 3v_<->_5v.LV, J1.pin8, Input.4
  N2: IC.5V, R1.Pin_1, Pwr.S, 3v_<->_5v.HV, J2.pin8
  N3: IC.A0, J1.pin2
  N4: IC.D0, J1.pin3
  N5: IC.D1, J2.pin3
  N6: IC.D2, J2.pin4
  N7: IC.D3, R2.Pin_1, J2.pin5
  N8: IC.D4, Input.3, J2.pin6
  N9: IC.D5, 3_3v_Relay.COIL2, 3v_<->_5v.TX2_LV, J1.pin4
  N10: IC.D6, 3v_<->_5v.RX2_LV, J1.pin5
  N11: IC.D7, 3v_<->_5v.RX_LV, J1.pin6
  N12: IC.D8, 3v_<->_5v.TX_LV, J1.pin7
  N13: IC.G, 5v_Power.pin2, R3.Pin_0, 3_3v_Relay.COIL1, Status.cathode, Power.cathode, 3v_<->_5v.GND, J2.pin7
  N14: IC.RST, J1.pin1
  N15: IC.RX, J2.pin2
  N16: IC.TX, J2.pin1
  N17: 5v_Power.pin1, Pwr.P
  N18: R1.Pin_0, Power.anode
  N19: R2.Pin_0, Status.anode
  N20: R3.Pin_1, Input.1
  N21: 3_3v_Relay.A, Relay_Out.pin3
  N22: 3_3v_Relay.C, Relay_Out.pin2
  N23: 3_3v_Relay.B, Relay_Out.pin1
  N24: 3v_<->_5v.TX_HV, 5v_Logic.pin1
  N25: 3v_<->_5v.RX_HV, 5v_Logic.pin2
  N26: 3v_<->_5v.RX2_HV, 5v_Logic.pin3
  N27: 3v_<->_5v.TX2_HV, 5v_Logic.pin4

notes:
  3v D8 D7 D6 D5 D0 A0 RST
  5v G  D4 D3 D2 D1 RX TX
  |_  \  _|
  TX1 RX1 TX0 RX0
  bubbles
  G 5v

custom parts:
  WeMos D1 Mini: The D1 mini is a mini wifi board based on ESP-8266EX.
